# Fritzing sketch schema (saved by Fritzing 0.9.2b)
breadboards: 1

parts:
  Raspberry_Pi_1 = Raspberry Pi 3 [part_number=RPI-3-V1.2]
  DHT1 = DHT11 Humitidy and Temperature Sensor
  R1 = Resistor [tolerance=±5% resistance=4.7k package="2010 [SMD]"]
  LED1 = smd LED [color="Red (633nm)" package="1206 [SMD]"]
  R2 = Resistor [tolerance=±5% resistance=220 package="0805 [SMD]"]

nets:
  3V3: Raspberry_Pi_1.3v3, DHT1.VDD, R1.Pin_0
  GND: Raspberry_Pi_1.GND, DHT1.GND
  N1: Raspberry_Pi_1.GIPO17, R2.Pin_1
  N2: Raspberry_Pi_1.GIPO14, DHT1.DATA, R1.Pin_1
  N3: LED1.anode, R2.Pin_0

custom parts:
  DHT11 Humitidy and Temperature Sensor: DHT11 Humidity and Temperature Sensor
